# Fritzing sketch alarmclock_mk1 (saved by Fritzing 0.9.3b)
breadboards: 2

parts:
  Bauteil1 = Arduino Nano (Rev3.0)
  Select_Encoder = Rotary Encoder [package=THT]
  Select_Button = Pushbutton [package="[THT]"]
  VCC1 = Battery block 9V
  J1 = Camdenboss CTB0158-4 [part_number=CTB0158-4 package=THT]
  SPKR1 = Loudspeaker
  Led_8x8_Display = LED Matrix - Serial Interface - Red/Green/Blue
  Radio = Digital FM Radio Receiver
  Snooze_Button = Pushbutton [package="[THT]"]
  Master_Switch = Pushbutton [package=THT]
  Amplifier = LM386 [package=dip08]
  C1 = Electrolytic Capacitor [capacitance=100µF voltage=10V package="100 mil [THT, electrolytic]"]
  C2 = Ceramic Capacitor [capacitance=100nF voltage=10V package="100 mil [THT, multilayer]"]
  C3 = Electrolytic Capacitor [capacitance=100µF package="100 mil [THT, electrolytic]"]
  R1 = Rotary Potentiometer (Small) [maximum_resistance=10kΩ package=THT]
  Phones_Out = rounded female pin header, 1 pin [form="♀ (female rounded)"]

nets:
  GND: Bauteil1.GND, Select_Encoder.EncoderPinC, Select_Button.Pin_3, Select_Button.Pin_4, J1.pin2, J1.pin3, Led_8x8_Display.GND, Radio.GND, Snooze_Button.Pin_1, Snooze_Button.Pin_2, Master_Switch.leg0, Amplifier.+IN, Amplifier.V-, C3.-, R1.leg2
  N1: Bauteil1.D2, Radio.!RST
  N2: Bauteil1.D5, Master_Switch.leg1
  N3: Bauteil1.D6, Select_Encoder.EncoderPinB
  N4: Bauteil1.D7, Select_Encoder.EncoderPinA
  N5: Bauteil1.D8, Select_Button.Pin_1, Select_Button.Pin_2
  N6: Bauteil1.D9, Snooze_Button.Pin_3, Snooze_Button.Pin_4
  N7: Bauteil1.D10, Led_8x8_Display.SCK
  N8: Bauteil1.D11/MOSI, Led_8x8_Display.CS
  N9: Bauteil1.D12/MISO, Led_8x8_Display.MOSI
  N10: Bauteil1.VIN, J1.pin4, Amplifier.V+, C3.+
  5V: Bauteil1.5V, Led_8x8_Display.VCC
  N11: Bauteil1.A5, Radio.SCLK
  N12: Bauteil1.A4, Radio.SDIO
  3V3: Bauteil1.3V3, Radio.3.3V
  N13: VCC1.-, J1.terminal_3
  N14: VCC1.+, J1.terminal_4
  N15: J1.pin1, C1.-
  N16: J1.terminal_1, SPKR1.pin2
  N17: J1.terminal_2, SPKR1.pin1
  N18: Amplifier.-IN, C2.1
  N19: Amplifier.OUT, C1.+
  N20: C2.0, R1.wiper
  N21: R1.leg1, Phones_Out.pin1
